# Fritzing sketch ATtiny85 ISP Plugin (saved by Fritzing 0.7.4b)
breadboards: 1

parts:
  J1 = female pin header, 2 pins [form="♀ (female)"]
  J2 = female pin header, 2 pins [form="♀ (female)"]
  J3 = female pin header, 2 pins [form="♀ (female)"]
  J4 = female pin header, 2 pins [form="♀ (female)"]
  J5 = female pin header, 2 pins [form="♀ (female)"]
  J6 = female pin header, 2 pins [form="♀ (female)"]
  J7 = female pin header, 2 pins [form="♀ (female)"]

nets:
  N1: J1.pin1, J4.pin1
  N2: J1.pin2, J5.pin1
  N3: J2.pin1, J5.pin2
  N4: J2.pin2, J4.pin2
  GND: J3.pin1, J7.pin2
  N5: J3.pin2, J6.pin1
