# Fritzing sketch EightDuino (saved by Fritzing 0.7.4b)
breadboards: 1

parts:
  ATmega328 = atmega328 [package=dip]
  ISP = shrouded pin header, 6 pins [form="♂ (shrouded male)"]
  EightDuino_by_mibus = Arduino
  RST = Pushbutton [package="[THT]"]  # not connected

nets:
  N1: ATmega328.RESET, ISP.pin3, EightDuino_by_mibus.RST
  N2: ATmega328.D0_(RX), EightDuino_by_mibus.D0RX
  N3: ATmega328.D1_(TX), EightDuino_by_mibus.D1TX
  N4: ATmega328.D2, EightDuino_by_mibus.D2
  N5: ATmega328.D3_(PWM), EightDuino_by_mibus.D3
  N6: ATmega328.D4, EightDuino_by_mibus.D4
  VCC: ATmega328.VCC, ATmega328.AVCC, ISP.pin6, EightDuino_by_mibus.+5V
  N7: ATmega328.D5_(PWM), EightDuino_by_mibus.D5
  N8: ATmega328.D6_(PWM), EightDuino_by_mibus.D6
  N9: ATmega328.D7, EightDuino_by_mibus.D7
  N10: ATmega328.D8, EightDuino_by_mibus.D8
  N11: ATmega328.D9_(PWM), EightDuino_by_mibus.D9
  N12: ATmega328.D10_(PWM), EightDuino_by_mibus.D10
  N13: ATmega328.D11_(PWM), ISP.pin5, EightDuino_by_mibus.D11
  N14: ATmega328.D12, ISP.pin1, EightDuino_by_mibus.D12
  N15: ATmega328.D13, ISP.pin2, EightDuino_by_mibus.D13
  N16: ATmega328.AREF, EightDuino_by_mibus.aref
  GND: ATmega328.GND#21, ISP.pin4, EightDuino_by_mibus.GND
  N17: ATmega328.A0, EightDuino_by_mibus.A0
  N18: ATmega328.A1, EightDuino_by_mibus.A1
  N19: ATmega328.A2, EightDuino_by_mibus.A2
  N20: ATmega328.A3, EightDuino_by_mibus.A3
  N21: ATmega328.A4, EightDuino_by_mibus.A4
  N22: ATmega328.A5, EightDuino_by_mibus.A5

notes:
  EightDuino by mibus
